# Fritzing sketch babyTamagotchi (saved by Fritzing 0.9.3b)

parts:
  Součástka1 = Arduino Pro Mini v13
  S2 = Pushbutton [part_number=Feed package=THT]
  S3 = Pushbutton [part_number=Play package=THT]
  U1 = LIPO-110mAh [package=lipo-110]
  TP1 = TP4056 [chip_label=TP4056 package="DIP (Dual Inline) [THT]"]
  Nokia_5110_LCD_Module1 = Nokia 5110 LCD
  R1 = Resistor [tolerance=±5% resistance=10k package=THT]
  R2 = Resistor [tolerance=±5% resistance=10k package=THT]

nets:
  N1: Součástka1.VCC, TP1.pin4, Nokia_5110_LCD_Module1.DN(MOSI), Nokia_5110_LCD_Module1.DN(MODI)_(out), R1.Pin_0
  N2: Součástka1.GND, S2.leg0, S3.leg0, TP1.pin5, Nokia_5110_LCD_Module1.LED, Nokia_5110_LCD_Module1.LED_(out)
  N3: Součástka1.A3, Nokia_5110_LCD_Module1.D/C_(out)
  N4: Součástka1.A2, Nokia_5110_LCD_Module1.RST_(out)
  N5: Součástka1.A1, Nokia_5110_LCD_Module1.SCE_(out)
  N6: Součástka1.A0, Nokia_5110_LCD_Module1.GND_(out)
  N7: Součástka1.D13/SCK, Nokia_5110_LCD_Module1.VCC, Nokia_5110_LCD_Module1.VCC_(out)
  N8: Součástka1.D5_PWM, S2.leg1, R2.Pin_1
  N9: Součástka1.D2, S3.leg1, R1.Pin_1
  N10: U1.+, TP1.pin3
  N11: U1.-, TP1.pin6

notes:
  Feed
  button
  Play
  button
  Both buttons
  for cleaning...

custom parts:
  TP4056: A DIP stand-in part for whatever IC you want. With 6 pins on a 300mil dual inline package (DIP) footprint.
  Nokia 5110 LCD: Nokia 5110 Graphic 84*48 LCD module such as the Sparkfun LCD-10168 or the clones from Ebay. There is example code for the Arduino available from the Sparkfun site in https://learn.sparkfun.com/tutorials/graphic-lcd-hookup-guide This is a 3.3V device, if you are running it from a 5V micro you need a 5V tolorant level translator such as the 74ahc367 to protect the signal imputs. Rafa G. did a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
